# Fritzing sketch ReallyBadController (saved by Fritzing 0.9.3b)
breadboards: 1

parts:
  Part1 = Arduino Uno (Rev3)
  hc-sr1 = hc-sr04
  Part2 = Thumb Joystick
  DS1 = DS18B20 1-Wire Temperature Sensor [part_number=DS18B20]
  R1 = Photocell (LDR) [package=THT]
  S1 = Momentary Switch [package=ksa_sealed_tac_switch]
  R3 = Resistor [tolerance=±5% resistance=10k package=THT]
  R4 = Resistor [tolerance=±5% resistance=10k package=THT]

nets:
  N1: Part1.A0, R1.pin_1, R4.Pin_0
  N2: Part1.A1, DS1.DQ
  N3: Part1.A2, Part2.HORZ
  N4: Part1.A3, Part2.VERT
  N5: Part1.D8, S1.1, R3.Pin_0
  N6: Part1.D6_PWM, hc-sr1.Echo
  N7: Part1.D7, hc-sr1.Trig
  VCC: Part1.5V, hc-sr1.VCC, Part2.VCC, DS1.VDD, R1.pin_0, S1.3
  GND: Part1.GND, hc-sr1.GND, Part2.GND, DS1.GND, R3.Pin_1, R4.Pin_1
